# Fritzing sketch wiring (saved by Fritzing 0.9.3b)
perfboards: 2

parts:
  Composant1 = Arduino Uno (Rev3)
  M1 = Stepper Motor - Bipolar  # not connected
  X1 = USB Connectors [package=usb-a-s-nosilk]
  J1 = Basic Servo
  X3 = USB Connectors [package=usb-a-s-nosilk]
  R1 = Rotary Potentiometer (Small) [maximum_resistance=100kΩ package=THT]

nets:
  N1: Composant1.D10_PWM/SS, J1.pulse
  N2: Composant1.D11_PWM/MOSI, R1.wiper
  N3: Composant1.5V, R1.leg1
  GND: Composant1.GND, X1.GND, R1.leg2
  N4: Composant1.VIN, X1.VBUS
  GND_2: J1.gnd, X3.GND
  N5: J1.vcc, X3.VBUS

notes:
  COM-W-V-U
  5-12V / GND
  NO PC
  brushless HDD motor
  motor controller
  5V - 2.5 A(6V)
  7-12V
  then 7-12V
  Control rotation
  Control orientation
  Absolute angle
  5-12V / GND / IN1 / IN2 / IN3 / IN4
